# Fritzing sketch FuelGauge (saved by Fritzing 0.9.3b)
circuit board: 8.46667cm x 5.64444cm
perfboards: 1

parts:
  LED3 = LED - 3mm [color="Yellow (595nm)" package="3 mm [THT]"]
  LED8 = LED - 3mm [color="Green (555nm)" package="3 mm [THT]"]
  LED9 = LED - 3mm [color="Green (555nm)" package="3 mm [THT]"]
  LED7 = LED - 3mm [color="Green (555nm)" package="3 mm [THT]"]
  LED10 = LED - 3mm [color="Green (555nm)" package="3 mm [THT]"]
  LED6 = LED - 3mm [color="Green (555nm)" package="3 mm [THT]"]
  LED5 = LED - 3mm [color="Yellow (595nm)" package="3 mm [THT]"]
  LED4 = LED - 3mm [color="Yellow (595nm)" package="3 mm [THT]"]
  LED1 = LED - 3mm [color="Red (633nm)" package="3 mm [THT]"]
  LED2 = LED - 3mm [color="Red (633nm)" package="3 mm [THT]"]
  LM3914 = IC, DIP package, 18 pins [chip_label=LM3914]
  R8 = Resistor [tolerance=±1% resistance=82 package=THT]
  R7 = Resistor [tolerance=±1% resistance=82 package=THT]
  R9 = Resistor [tolerance=±1% resistance=82 package=THT]
  R10 = Resistor [tolerance=±1% resistance=82 package=THT]
  R6 = Resistor [tolerance=±1% resistance=82 package=THT]
  R5 = Resistor [tolerance=±1% resistance=330 package=THT]
  R4 = Resistor [tolerance=±1% resistance=330 package=THT]
  R3 = Resistor [tolerance=±1% resistance=330 package=THT]
  R2 = Resistor [tolerance=±1% resistance=220 package=THT]
  R1 = Resistor [tolerance=±1% resistance=220 package=THT]

nets:
  N1: LED3.cathode, R3.Pin_0
  3.3V: LED3.anode, LED8.anode, LED9.anode, LED7.anode, LED10.anode, LED6.anode, LED5.anode, LED4.anode, LED1.anode, LED2.anode
  N2: LED8.cathode, R8.Pin_0
  N3: LED9.cathode, R9.Pin_0
  N4: LED7.cathode, R7.Pin_0
  N5: LED10.cathode, R10.Pin_0
  N6: LED6.cathode, R6.Pin_0
  N7: LED5.cathode, R5.Pin_0
  N8: LED4.cathode, R4.Pin_0
  N9: LED1.cathode, R1.Pin_0
  N10: LED2.cathode, R2.Pin_0
  N11: LM3914.pin1, R1.Pin_1
  GND: LM3914.pin2, LM3914.pin4
  9V: LM3914.pin3
  5V: LM3914.pin5
  N12: LM3914.pin10, R10.Pin_1
  N13: LM3914.pin11, R9.Pin_1
  N14: LM3914.pin12, R8.Pin_1
  N15: LM3914.pin13, R7.Pin_1
  N16: LM3914.pin14, R6.Pin_1
  N17: LM3914.pin15, R5.Pin_1
  N18: LM3914.pin16, R4.Pin_1
  N19: LM3914.pin17, R3.Pin_1
  N20: LM3914.pin18, R2.Pin_1

notes:
  All LEDs' anodes connected to 3.3V
